# Fritzing sketch musicbox (saved by Fritzing 0.9.4)

parts:
  MCU1 = Raspberry Pi Zero
  Part1 = RFID-RC522-v3
  R1 = Resistor [tolerance=±5% resistance=1k package="0805 [SMD]"]
  LED1 = smd LED [color="Red (633nm)" package="0603 [SMD]"]
  L6 = Inductor [package="1206 [SMD]"]
  C3 = Capacitor Polarized [package=panasonic_d]
  C4 = Capacitor Polarized [package=panasonic_d]
  shutdown_button = Round Pushbutton
  vol-_button = Round Pushbutton
  Part2 = InvenSense MPU6050
  vol+_button = Round Pushbutton

nets:
  3.3V: MCU1.pin_1, MCU1.pin_17, Part1.3.3V, Part2.VCC
  N1: MCU1.pin_2, C3.+, C4.+
  N2: MCU1.pin_3, Part2.SDA
  N3: MCU1.pin_5, Part2.SCL
  GND: MCU1.pin_6, MCU1.pin_9, MCU1.pin_14, MCU1.pin_20, MCU1.pin_25, MCU1.pin_30, MCU1.pin_34, Part1.GND, LED1.cathode, L6.pin_0, shutdown_button.leg0, vol-_button.leg1, Part2.GND, vol+_button.leg1
  N4: MCU1.pin_7, shutdown_button.leg1
  N5: MCU1.pin_8, R1.Pin_0
  N6: MCU1.pin_18, Part1.IRQ
  N7: MCU1.pin_19, Part1.MOSI
  N8: MCU1.pin_21, Part1.MISO
  N9: MCU1.pin_22, Part1.RST
  N10: MCU1.pin_23, Part1.SCK
  N11: MCU1.pin_24, MCU1.pin_38, Part1.SDA
  N12: MCU1.pin_29, vol-_button.leg0
  N13: MCU1.pin_33, vol+_button.leg0
  N14: R1.Pin_1, LED1.anode
  N15: L6.pin_1, C3.-, C4.-

notes:
  pink connections indicate usage of HifiBerry Miniamp

custom parts:
  RFID-RC522-v3: A simple China made RFID-RC522 Reader (6x4 cm); do check the pin labels, as this is a MFRC522 based clone.
